# Fritzing sketch Sketch (saved by Fritzing 0.9.5d)

parts:
  Pompa_Air_Pemanas = DC Motor
  Power_Supply_12V_AC/DC = prefix0000 [part_number=S-350-60]
  Pompa_Air_Galon = water pump/motor
  Power_Step_Down = 电源转换模块
  Module_Relay_3_Channel_12V = 3 channel relay module
  Sensor_Suhu_Mesin = DS18B20 1-Wire Temperature Sensor [part_number=DS18B20]
  part = ESP32-S2-DevKitM-1 [part_number=ESP32-S2-DevKitM-1]
  Lampu_Indikator_1 = LEDs [package=led10mm]
  R1 = Resistor [tolerance=±5% resistance=220 package="0402 [SMD]"]
  Tombol_Isi_Ulang_Kopi = SWITCH-MOMENTARY-2 [package=tactile-pth]
  Tombol_Sajikan_Kopi = SWITCH-MOMENTARY-2 [package=tactile-pth]
  Switch = Round Pushbutton
  AC_Input = AC Power [frequency=60]
  Selenoid_Valve_Katup_Tuang_Kopi = Plastic Solenoid Valve
  Katup_Kopi = Dagu DGServo 9g (Top view) [part_number=RS001B]
  Katup_Gula = Dagu DGServo 9g (Top view) [part_number=RS001B]
  Motor_Pengaduk = DC Motor
  Module_Relay_1_Channel_12V = 1 chan 5v relay module
  LED_Indikator_2 = LEDs [package=led10mm]
  R2 = Resistor [tolerance=±5% resistance=220 package="0402 [SMD]"]
  LED_Indikator_3 = LEDs [package=led10mm]
  R3 = Resistor [tolerance=±5% resistance=220 package="0402 [SMD]"]

nets:
  N1: Pompa_Air_Pemanas.pin_1, Module_Relay_3_Channel_12V.Pin_12
  N2: Pompa_Air_Pemanas.pin_2, Power_Supply_12V_AC/DC.connector5, Pompa_Air_Galon.pin_2, Selenoid_Valve_Katup_Tuang_Kopi.no_name_yet#2, Motor_Pengaduk.pin_2
  N3: Power_Supply_12V_AC/DC.connector0, Power_Step_Down.Pin_10, Power_Step_Down.Pin_12, Module_Relay_1_Channel_12V.pin_5
  GND: Power_Supply_12V_AC/DC.connector6, Power_Step_Down.Pin_3, Power_Step_Down.Pin_6, Power_Step_Down.Pin_9, Katup_Kopi.gnd, Katup_Gula.gnd
  N4: Power_Supply_12V_AC/DC.connector7, AC_Input.V+
  N5: Power_Supply_12V_AC/DC.connector8, Switch.leg1
  N6: Pompa_Air_Galon.pin_1, Module_Relay_3_Channel_12V.Pin_15
  N7: Power_Step_Down.Pin_16, Power_Step_Down.Pin_18, part.5V
  N8: Module_Relay_3_Channel_12V.Pin_2, part.33
  N9: Module_Relay_3_Channel_12V.Pin_3, part.26
  N10: Module_Relay_3_Channel_12V.Pin_4, part.21
  N11: Module_Relay_3_Channel_12V.Pin_6, Sensor_Suhu_Mesin.GND, part.G-21, part.G-42, Lampu_Indikator_1.C, Module_Relay_1_Channel_12V.pin_2, LED_Indikator_2.C, LED_Indikator_3.C
  VCC: Module_Relay_3_Channel_12V.Pin_7, Sensor_Suhu_Mesin.VDD, part.3V3, Katup_Kopi.vcc, Katup_Gula.vcc, Module_Relay_1_Channel_12V.pin_1
  N12: Module_Relay_3_Channel_12V.Pin_9, Motor_Pengaduk.pin_1
  N13: Sensor_Suhu_Mesin.DQ, part.39
  N14: part.42, R1.Pin_1
  N15: part.3, Tombol_Isi_Ulang_Kopi.1
  N16: part.4, Tombol_Sajikan_Kopi.1
  N17: part.6, Module_Relay_1_Channel_12V.pin_3
  N18: part.16, Katup_Gula.pulse
  N19: part.17, Katup_Kopi.pulse
  N20: Lampu_Indikator_1.A, R1.Pin_0
  N21: Tombol_Isi_Ulang_Kopi.2, R2.Pin_0
  N22: Tombol_Sajikan_Kopi.2, R3.Pin_0
  N23: Switch.leg0, AC_Input.V-
  N24: Selenoid_Valve_Katup_Tuang_Kopi.no_name_yet#1, Module_Relay_1_Channel_12V.pin_4
  N25: LED_Indikator_2.A, R2.Pin_1
  N26: LED_Indikator_3.A, R3.Pin_1

custom parts:
  water pump/motor: WATER PUMP BY ARDUBLOCKTR
  电源转换模块: DC-DC 12V To 3.3V 5V Buck Step down Power Supply Module For Arduino
  3 channel relay module: This product is 3 channel self-locking and interlocking relay function.Keep button on 3 second when set tirgger level. it will automatic switchover self-locking and interlock function. 3 channel self-locking function:Press the corresponding button,the corresppond relay on,press again,relay off. 3 channel interlock function:Press the corresponding button,the corresppond relay on,but other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
  ESP32-S2-DevKitM-1: The DOIT Esp32 DevKit v1 is one of the development board created by DOIT to evaluate the ESP-WROOM-32 module. It is based on the ESP32 microcontroller that boasts Wifi, Bluetooth, Ethernet and Low Power support all in a single chip. (vanepp) Feb 2021: converted to ESP32-S2-DevKitM-1. This module is 42pins long (2x21) and 11 pins width.
  1 chan 5v relay module: 1 Channel 5V Relay Module Board Shield with Optocoupler Support High and Low Level Trigger for Arduino.
